# Fritzing sketch TimberManRxControl (saved by Fritzing 0.9.3b)
breadboards: 1
stripboards: 1

parts:
  U1 = XD-RF-5V [package=THT]
  IC1 = MICROCONTROLLER [package=dil28-3-zif_socket]
  S1 = Pushbutton [package="[THT]"]
  L1 = Inductor [package="400 mil [THT]"]
  L2 = Inductor [package="400 mil [THT]"]
  L3 = Inductor [package="400 mil [THT]"]
  R1 = Resistor [tolerance=±5% resistance=1k package=THT]
  Y1 = CRYSTAL [package=hc49up]
  C1 = Ceramic Capacitor [capacitance="100 nF" package="0805 [SMD, multilayer]"]
  C2 = Ceramic Capacitor [capacitance="100 nF" package="0805 [SMD, multilayer]"]
  Componente1 = FTDI Basic Programmer
  IC2 = MICROCONTROLLER [package=dil28-3-zif_socket]
  U2 = XD-RF-5V [package=THT]
  L4 = Inductor [package="400 mil [THT]"]
  L5 = Inductor [package="400 mil [THT]"]  # not connected
  L6 = Inductor [package="400 mil [THT]"]  # not connected
  L7 = Inductor [package="400 mil [THT]"]  # not connected
  S2 = Pushbutton [package="[THT]"]
  R2 = Resistor [tolerance=±5% resistance=1k package=THT]
  Y2 = CRYSTAL [package=hc49up]
  C3 = Ceramic Capacitor [capacitance="100 nF" package="0805 [SMD, multilayer]"]
  C4 = Ceramic Capacitor [capacitance="100 nF" package="0805 [SMD, multilayer]"]
  Componente2 = FTDI Basic Programmer

nets:
  N1: U1.VCC, IC1.PB7(XTAL2_TOSC2), IC1.PB5(SCK), Y1.2, C1.0, C1.1
  N2: U1.DATA#1, IC1.PD5(T1), IC1.PB4(MISO)
  N3: U1.DATA#2, IC1.PD6(AIN0), IC1.PB3(MOSI_OC2)
  N4: U1.GND, IC1.PD7(AIN1), IC1.PB2(SS_OC1B)
  N5: U1.Attenna, L1.pin_0, L1.pin_1, L2.pin_1, L3.pin_1
  N6: IC1.PC6(_RESET), IC1.PC5(ADC5_SCL), R1.Pin_0, Componente1.TXO
  N7: IC1.PD0(RXD), IC1.PC4(ADC4_SDA), Componente1.RXI
  N8: IC1.PD1(TXD), IC1.PC3(ADC3)
  N9: IC1.PD2(INT0), IC1.PC2(ADC2)
  N10: IC1.PD3(INT1), IC1.VCC, IC1.AGND, IC1.PC1(ADC1), R1.Pin_1, Componente1.POWER
  N11: IC1.PD4(XCK_T0), IC1.PC0(ADC0)
  GND: IC1.GND, IC1.AREF, Componente1.GND
  N12: IC1.PB6(XTAL1_TOSC1), IC1.AVCC, Y1.1, C2.0, C2.1
  N13: IC1.PB0(ICP), IC1.PB1(OC1A)
  N14: S1.Pin_1, S1.Pin_2
  N15: S1.Pin_3, S1.Pin_4
  N16: IC2.PC6(_RESET), S2.Pin_1, S2.Pin_2, R2.Pin_0, Componente2.TXO
  N17: IC2.PD0(RXD), Componente2.RXI
  N18: IC2.PD3(INT1), IC2.VCC, R2.Pin_1, Componente2.POWER
  GND_2: IC2.GND, S2.Pin_3, S2.Pin_4, C3.1, C4.0, Componente2.GND
  N19: IC2.PB6(XTAL1_TOSC1), Y2.1, C4.1
  N20: IC2.PB7(XTAL2_TOSC2), Y2.2, C3.0
  N21: IC2.PB3(MOSI_OC2), U2.DATA#2
  N22: IC2.AVCC, U2.VCC
  N23: IC2.AGND, U2.GND
  N24: U2.Attenna, L4.pin_1

custom parts:
  XD-RF-5V: This is 433Mhz RF transmitter with receiver kit for Arduino ARM MCU wireless Application environment: Remote control switch, receiver module, motorcycles, automobile anti-theft products, home security products, electric doors, shutter doors, windows, remote control socket, remote control LED, remote audio remote control electric doors, garage door remote control, remote control retractable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
